# Fritzing sketch MP1 Sketch (saved by Fritzing 0.9.3b)
breadboards: 1

parts:
  M1 = Stepper Motor - Bipolar
  Pololu_A1 = Pololu A4988 [package=SO16]
  Part1 = Arduino Mega 2560 (Rev3)
  VCC1 = Battery block 9V

nets:
  N1: M1.A, Pololu_A1.1B
  N2: M1.C, Pololu_A1.1A
  N3: M1.B, Pololu_A1.2A
  N4: M1.D, Pololu_A1.2B
  N5: Pololu_A1.MS1, Part1.D8_PWM
  N6: Pololu_A1.MS2, Part1.D9_PWM
  N7: Pololu_A1.MS3, Part1.D10_PWM
  N8: Pololu_A1.RESET, Pololu_A1.SLEEP
  N9: Pololu_A1.STEP, Part1.D3_PWM
  N10: Pololu_A1.DIR, Part1.D4_PWM
  N11: Pololu_A1.GND#8, Part1.GND
  VDD: Pololu_A1.VDD, Part1.5V
  N12: Pololu_A1.GND#14, VCC1.-
  N13: Pololu_A1.VMOT, VCC1.+
